# Fritzing sketch koblingsArk (saved by Fritzing 0.9.3b)
breadboards: 2

parts:
  U1 = MAX7219 [package=dil24]
  Disp1 = LBT2088AH [part_number=1588AS]
  R1 = Resistor [tolerance=±5% resistance=100 package="2010 [SMD]"]
  R2 = Resistor [tolerance=±5% resistance=100 package="2512 [SMD]"]
  R3 = Resistor [tolerance=±5% resistance=100 package="2512 [SMD]"]
  Part2 = Arduino Uno (Rev3) - ICSP

nets:
  N1: U1.DIN, Part2.ICSP_MISO, Part2.D12/MISO
  N2: U1.DIG0, Disp1.pin1
  N3: U1.DIG4, Disp1.pin_9
  GND: U1.GND, U1.GND2, Part2.GND
  N4: U1.DIG6, Disp1.pin_10
  N5: U1.DIG2, Disp1.pin_16
  N6: U1.DIG3, Disp1.pin_4
  N7: U1.DIG7, Disp1.pin_13
  N8: U1.DIG5, Disp1.pin_15
  N9: U1.DIG1, Disp1.pin_6
  N10: U1.LOAD, Part2.D10_PWM/SS
  N11: U1.CLK, Part2.D11_PWM/MOSI
  N12: U1.SEGA, Disp1.pin_11
  N13: U1.SEGF, Disp1.pin_7
  N14: U1.SEGB, Disp1.pin_12
  N15: U1.SEGG, Disp1.pin_8
  N16: U1.ISET, R3.Pin_0
  VCC: U1.VCC, Part2.5V
  N17: U1.SEGC, Disp1.pin2
  N18: U1.SEGE, Disp1.pin_3
  N19: U1.SEGDP, Disp1.pin_5
  N20: U1.SEGD, Disp1.pin_14
  N21: R1.Pin_0, R2.Pin_1
  N22: R2.Pin_0, R3.Pin_1
